# Fritzing sketch paeiot-sensor-one (saved by Fritzing 0.9.3b)
circuit board: 2.50493cm x 4.08159cm
breadboards: 1

parts:
  M1 = Arduino MKR WAN 1300
  AM1 = AM2302 Humidity and Temperature Sensor
  AM2 = AM2302 Humidity and Temperature Sensor
  J1 = male pin header, 3 pins [form="♂ (male)"]
  J2 = male pin header, 3 pins [form="♂ (male)"]
  J3 = female pin header, 3 pins [form="♀ (female)"]
  J4 = female pin header, 3 pins [form="♀ (female)"]
  R1 = Resistor [tolerance=±5% resistance=220 package=THT]
  LED1 = LED - 3mm [color="Green (570nm)" package="3 mm [THT]"]

nets:
  N1: M1.0, R1.Pin_1
  N2: M1.~2, J1.pin1
  N3: M1.~3, J2.pin1
  N4: M1.GND, J1.pin3, J2.pin3, LED1.cathode
  N5: M1.VCC, J1.pin2, J2.pin2
  N6: AM1.VDD, J3.pin2
  N7: AM1.DATA, J3.pin1
  N8: AM1.GND, J3.pin3
  N9: AM2.VDD, J4.pin2
  N10: AM2.DATA, J4.pin1
  N11: AM2.GND, J4.pin3
  N12: R1.Pin_0, LED1.anode

notes:
  paeiot
  sensor one
  v1.1 02/10/2021

custom parts:
  Arduino MKR WAN 1300: Arduino MKR WAN 1300 ,Cortex-M0 CPU with LoRa connectivity. CPU: SAMD21 Cortex-M0+ 32bit low power ARM MCU, 256 KB Flash 32K SRAM. Note: pins 28 and 29 (-VBAT and +VBAT) aren't defined in PCB view, because they are terminal blocks and don't connect to the pcb. Parts Editor will complain about unassigned pins but it is safe to ignore those 2 pins.
